# Fritzing sketch breadboard (saved by Fritzing 0.9.3b)
breadboards: 1

parts:
  Part1 = SparkFun ESP8266 Thing  # not connected
  RHT1 = Humidity and Temperature Sensor RHT03
  R1 = Resistor [tolerance=±5% resistance=10k package=THT]

nets:
  N1: RHT1.Vcc, R1.Pin_0
  N2: RHT1.Data-signal, R1.Pin_1
